// Logisim project Project.circ as structural Verilog: 15 circuits, main circuit main
module main (
  input  Clear,
  input  Clear_2,
  input  Clock,
  output [15:0] out_4,
  output out_5,
  output out_6
);

  wire ALU_Control, CompareSignal, ImmediateSignal, InstReadSignal, JumpCheck, JumpSignal, Load,
       MemWriteSignal, not_1_out, PCReadSignal, RegisterWriteSignal;
  wire [1:0] ALUClock;
  wire [2:0] DST, multiplexer_1_out, multiplexer_2_out, OP1, OP2, SR1, SR2;
  wire [9:0] Jump_Address, LD_ST_Address, pc_register_1_pc_address;
  wire [15:0] ALU_Result, DataMemoryValue, Immediate_Address, multiplexer_3_out, OP1Value, OP2Value,
       Op2Value_t, register_file_1_output_data, register_file_1_output_data2, RegOut1, RegOut2, rom_1_data;

  Arithmetic_Logic_Unit arithmetic_logic_unit_1 (
    .SR1(RegOut1), .SR2(RegOut2), .Result(ALU_Result), .op(ALUClock), .Immediate(Immediate_Address));  // open: Carry_out, Carry_out_2
  PC_Register pc_register_1 (
    .Jump_Address(Jump_Address), .Enable(PCReadSignal), .PC_Address(pc_register_1_pc_address),
    .Clear(Clear_2), .AddressSelect(JumpSignal), .Clock(Clock));
  // Probe on pc_register_1_pc_address
  ROM #(.addrWidth(10), .dataWidth(16)) rom_1 (.addr(pc_register_1_pc_address), .data(rom_1_data));  // open: sel
  Multiplexer #(.width(3)) multiplexer_1 (
    .in0(SR1), .in1(OP1), .out(multiplexer_1_out), .sel(CompareSignal));  // open: en
  Multiplexer #(.width(3)) multiplexer_2 (
    .in0(SR2), .in1(OP2), .out(multiplexer_2_out), .sel(CompareSignal));  // open: en
  Multiplexer #(.width(16)) multiplexer_3 (
    .in0(DataMemoryValue), .in1(ALU_Result), .out(multiplexer_3_out), .sel(not_1_out));  // open: en
  not not_1 (not_1_out, Load);
  // Probe on rom_1_data
  Register_File register_file_1 (
    .write_register(DST), .read_register(multiplexer_1_out), .write_data(multiplexer_3_out),
    .output_data(register_file_1_output_data), .write_enable(RegisterWriteSignal), .clock(Clock),
    .read_register2(multiplexer_2_out), .output_data2(register_file_1_output_data2));
  Register #(.width(16)) register_1 (.D(rom_1_data), .en(InstReadSignal), .Q(out_4), .clk(Clock), .clr(Clear));
  Demultiplexer #(.width(16)) demultiplexer_1 (
    .out0(RegOut1), .out1(OP1Value), .in(register_file_1_output_data), .sel(CompareSignal));  // open: en
  Demultiplexer #(.width(16)) demultiplexer_2 (
    .out0(RegOut2), .out1(Op2Value_t), .in(register_file_1_output_data2), .sel(CompareSignal));  // open: en
  RAM #(.addrWidth(10), .dataWidth(16), .bus("separate")) ram_1 (
    .addr(LD_ST_Address), .din(RegOut1), .data(DataMemoryValue), .str(MemWriteSignal), .clk(Clock), .ld(Load));  // open: sel, clr
  Control_Unit control_unit_1 (
    .Input(out_4), .in_3(Clock), .CMPOP1(OP1Value), .CMPOP2(OP2Value), .SR2(SR2), .JumpSignal(JumpSignal),
    .ImmediateSignal(ImmediateSignal), .instReadSignal(InstReadSignal), .DST(DST),
    .pcReadSignal(PCReadSignal), .ZF(out_5), .CF(out_6), .memWriteSignal(MemWriteSignal),
    .Compare(CompareSignal), .Load(Load), .registerWriteSignal(RegisterWriteSignal), .out_21(ALUClock),
    .Jump_Address(Jump_Address), .LD_ST_Address(LD_ST_Address), .SR1(SR1),
    .Immediate_Address(Immediate_Address), .OP1(OP1), .OP2(OP2), .AluControl(ALU_Control),
    .JumpCheck(JumpCheck));
  // Probe on Immediate_Address

  // Other names for the same wires on the sheet: InstructionInput[15:0] = out_4

  // Notes on the sheet:
  //   ALU
  //   PC REGISTER
  //   contents of rom_1 (hex, n*v repeats v):
  //   7006 4205 1442 1c42 30c6 20c5 ac4 5c04 6142 b005 c006
  //   REGISTER FILE
  //   CONTROL UNIT
endmodule

module Half_Adder (
  input  a,
  input  b,
  output Carry_out,
  output Sum
);

  and and_1 (Carry_out, b, a);
  xor xor_1 (Sum, a, b);
endmodule

module Full_Adder (
  input  Carry_in,
  input  b,
  input  a,
  output Sum,
  output Carry_out
);

  wire and_1_out, and_2_out, and_3_out;

  xor xor_1 (Sum, Carry_in, b, a);
  and and_1 (and_1_out, Carry_in, b);
  and and_2 (and_2_out, Carry_in, a);
  and and_3 (and_3_out, b, a);
  or or_1 (Carry_out, and_1_out, and_2_out, and_3_out);
endmodule

module _16_Bit_Adder (
  input  [15:0] a,
  input  [15:0] b,
  output [15:0] Sum,
  output carry_out
);

  wire full_adder_1_carry_out, full_adder_2_carry_out, full_adder_3_carry_out, full_adder_4_carry_out,
       full_adder_5_carry_out, full_adder_6_carry_out, full_adder_7_carry_out, full_adder_8_carry_out,
       full_adder_9_carry_out, full_adder_10_carry_out, full_adder_11_carry_out, full_adder_12_carry_out,
       full_adder_13_carry_out, full_adder_14_carry_out, half_adder_1_carry_out;

  Half_Adder half_adder_1 (.a(a[0]), .b(b[0]), .Carry_out(half_adder_1_carry_out), .Sum(Sum[0]));
  Full_Adder full_adder_1 (
    .Carry_in(half_adder_1_carry_out), .a(a[1]), .b(b[1]), .Sum(Sum[1]), .Carry_out(full_adder_1_carry_out));
  Full_Adder full_adder_2 (
    .Carry_in(full_adder_1_carry_out), .a(a[2]), .b(b[2]), .Sum(Sum[2]), .Carry_out(full_adder_2_carry_out));
  Full_Adder full_adder_3 (
    .Carry_in(full_adder_2_carry_out), .a(a[3]), .b(b[3]), .Sum(Sum[3]), .Carry_out(full_adder_3_carry_out));
  Full_Adder full_adder_4 (
    .Carry_in(full_adder_3_carry_out), .a(a[4]), .b(b[4]), .Sum(Sum[4]), .Carry_out(full_adder_4_carry_out));
  Full_Adder full_adder_5 (
    .Carry_in(full_adder_4_carry_out), .a(a[5]), .b(b[5]), .Sum(Sum[5]), .Carry_out(full_adder_5_carry_out));
  Full_Adder full_adder_6 (
    .Carry_in(full_adder_5_carry_out), .a(a[6]), .b(b[6]), .Sum(Sum[6]), .Carry_out(full_adder_6_carry_out));
  Full_Adder full_adder_7 (
    .Carry_in(full_adder_6_carry_out), .a(a[7]), .b(b[7]), .Sum(Sum[7]), .Carry_out(full_adder_7_carry_out));
  Full_Adder full_adder_8 (
    .Carry_in(full_adder_7_carry_out), .a(a[8]), .b(b[8]), .Sum(Sum[8]), .Carry_out(full_adder_8_carry_out));
  Full_Adder full_adder_9 (
    .Carry_in(full_adder_8_carry_out), .a(a[9]), .b(b[9]), .Sum(Sum[9]), .Carry_out(full_adder_9_carry_out));
  Full_Adder full_adder_10 (
    .Carry_in(full_adder_9_carry_out), .a(a[10]), .b(b[10]), .Sum(Sum[10]),
    .Carry_out(full_adder_10_carry_out));
  Full_Adder full_adder_11 (
    .Carry_in(full_adder_10_carry_out), .a(a[11]), .b(b[11]), .Sum(Sum[11]),
    .Carry_out(full_adder_11_carry_out));
  Full_Adder full_adder_12 (
    .Carry_in(full_adder_11_carry_out), .a(a[12]), .b(b[12]), .Sum(Sum[12]),
    .Carry_out(full_adder_12_carry_out));
  Full_Adder full_adder_13 (
    .Carry_in(full_adder_12_carry_out), .a(a[13]), .b(b[13]), .Sum(Sum[13]),
    .Carry_out(full_adder_13_carry_out));
  Full_Adder full_adder_14 (
    .Carry_in(full_adder_13_carry_out), .a(a[14]), .b(b[14]), .Sum(Sum[14]),
    .Carry_out(full_adder_14_carry_out));
  Full_Adder full_adder_15 (
    .Carry_in(full_adder_14_carry_out), .a(a[15]), .b(b[15]), .Sum(Sum[15]), .Carry_out(carry_out));

  // Notes on the sheet:
  //   Bit-0
  //   Bit-1
  //   Bit-2
  //   Bit-3
  //   Bit-4
  //   Bit-5
  //   Bit-6
  //   Bit-7
  //   Bit-8
  //   Bit-9
  //   Bit-10
  //   Bit-11
  //   Bit-12
  //   Bit-13
  //   Bit-14
  //   Bit-15
endmodule

// Imm
module Arithmetic_Logic_Unit (
  input  [15:0] SR1,
  input  [1:0] op,
  input  [15:0] SR2,
  input  [15:0] Immediate,
  output [15:0] Result,
  output Carry_out,
  output Carry_out_2
);

  wire [15:0] and_1_out, and_2_out, n16_bit_adder_1_sum, n16_bit_adder_2_sum;

  assign and_1_out = SR1 & SR2;  // AND_Gate and_1, 16 bits wide
  _16_Bit_Adder u_16_bit_adder_1 (.a(SR1), .Sum(n16_bit_adder_1_sum), .b(SR2), .carry_out(Carry_out));
  assign and_2_out = SR1 & Immediate;  // AND_Gate and_2, 16 bits wide
  _16_Bit_Adder u_16_bit_adder_2 (.a(SR1), .Sum(n16_bit_adder_2_sum), .b(Immediate), .carry_out(Carry_out_2));
  Multiplexer #(.select(2), .width(16)) multiplexer_1 (
    .in0(and_1_out), .in1(n16_bit_adder_1_sum), .in2(and_2_out), .in3(n16_bit_adder_2_sum), .out(Result),
    .sel(op));  // open: en

  // Notes on the sheet:
  //   16 Bit Adder
  //   16 Bit Adder
endmodule

module Half_Comparator (
  input  a,
  input  b,
  output gt,
  output lt,
  output eq
);

  wire not_1_out, not_2_out;

  not not_1 (not_1_out, b);
  not not_2 (not_2_out, a);
  and and_1 (gt, a, not_1_out);
  and and_2 (lt, not_2_out, b);
  xnor xnor_1 (eq, a, b);
endmodule

module Full_Comparator (
  input  a,
  input  b,
  input  gtin,
  input  ltin,
  input  eqin,
  output gtout,
  output ltout,
  output eqout
);

  wire and_1_out, and_2_out, not_1_out, not_2_out, xnor_1_out;

  not not_1 (not_1_out, b);
  not not_2 (not_2_out, a);
  and and_1 (and_1_out, a, eqin, not_1_out);
  and and_2 (and_2_out, not_2_out, eqin, b);
  xnor xnor_1 (xnor_1_out, a, b);
  or or_1 (gtout, and_1_out, gtin);
  or or_2 (ltout, and_2_out, ltin);
  and and_3 (eqout, xnor_1_out, eqin);
endmodule

module _16_Bit_Comparator (
  input  [15:0] a,
  input  [15:0] b,
  output gt,
  output lt,
  output eq
);

  wire full_comparator_1_eqout, full_comparator_1_gtout, full_comparator_1_ltout, full_comparator_2_eqout,
       full_comparator_2_gtout, full_comparator_2_ltout, full_comparator_3_eqout, full_comparator_3_gtout,
       full_comparator_3_ltout, full_comparator_4_eqout, full_comparator_4_gtout, full_comparator_4_ltout,
       full_comparator_5_eqout, full_comparator_5_gtout, full_comparator_5_ltout, full_comparator_6_eqout,
       full_comparator_6_gtout, full_comparator_6_ltout, full_comparator_7_eqout, full_comparator_7_gtout,
       full_comparator_7_ltout, full_comparator_8_eqout, full_comparator_8_gtout, full_comparator_8_ltout,
       full_comparator_9_eqout, full_comparator_9_gtout, full_comparator_9_ltout, full_comparator_10_eqout,
       full_comparator_10_gtout, full_comparator_10_ltout, full_comparator_11_eqout,
       full_comparator_11_gtout, full_comparator_11_ltout, full_comparator_12_eqout,
       full_comparator_12_gtout, full_comparator_12_ltout, full_comparator_13_eqout,
       full_comparator_13_gtout, full_comparator_13_ltout, full_comparator_14_eqout,
       full_comparator_14_gtout, full_comparator_14_ltout, Half_Comparator_eq, Half_Comparator_gt,
       Half_Comparator_lt;

  Half_Comparator Half_Comparator (
    .a(a[15]), .b(b[15]), .gt(Half_Comparator_gt), .lt(Half_Comparator_lt), .eq(Half_Comparator_eq));
  Full_Comparator full_comparator_1 (
    .a(a[14]), .b(b[14]), .gtin(Half_Comparator_gt), .ltin(Half_Comparator_lt), .eqin(Half_Comparator_eq),
    .gtout(full_comparator_1_gtout), .ltout(full_comparator_1_ltout), .eqout(full_comparator_1_eqout));
  Full_Comparator full_comparator_2 (
    .a(a[12]), .b(b[12]), .gtin(full_comparator_3_gtout), .ltin(full_comparator_3_ltout),
    .eqin(full_comparator_3_eqout), .gtout(full_comparator_2_gtout), .ltout(full_comparator_2_ltout),
    .eqout(full_comparator_2_eqout));
  Full_Comparator full_comparator_3 (
    .a(a[13]), .b(b[13]), .gtin(full_comparator_1_gtout), .ltin(full_comparator_1_ltout),
    .eqin(full_comparator_1_eqout), .gtout(full_comparator_3_gtout), .ltout(full_comparator_3_ltout),
    .eqout(full_comparator_3_eqout));
  Full_Comparator full_comparator_4 (
    .a(a[11]), .b(b[11]), .gtin(full_comparator_2_gtout), .ltin(full_comparator_2_ltout),
    .eqin(full_comparator_2_eqout), .gtout(full_comparator_4_gtout), .ltout(full_comparator_4_ltout),
    .eqout(full_comparator_4_eqout));
  Full_Comparator full_comparator_5 (
    .a(a[10]), .b(b[10]), .gtin(full_comparator_4_gtout), .ltin(full_comparator_4_ltout),
    .eqin(full_comparator_4_eqout), .gtout(full_comparator_5_gtout), .ltout(full_comparator_5_ltout),
    .eqout(full_comparator_5_eqout));
  Full_Comparator full_comparator_6 (
    .a(a[9]), .b(b[9]), .gtin(full_comparator_5_gtout), .ltin(full_comparator_5_ltout),
    .eqin(full_comparator_5_eqout), .gtout(full_comparator_6_gtout), .ltout(full_comparator_6_ltout),
    .eqout(full_comparator_6_eqout));
  Full_Comparator full_comparator_7 (
    .a(a[8]), .b(b[8]), .gtin(full_comparator_6_gtout), .ltin(full_comparator_6_ltout),
    .eqin(full_comparator_6_eqout), .gtout(full_comparator_7_gtout), .ltout(full_comparator_7_ltout),
    .eqout(full_comparator_7_eqout));
  Full_Comparator full_comparator_8 (
    .a(a[6]), .b(b[6]), .gtin(full_comparator_9_gtout), .ltin(full_comparator_9_ltout),
    .eqin(full_comparator_9_eqout), .gtout(full_comparator_8_gtout), .ltout(full_comparator_8_ltout),
    .eqout(full_comparator_8_eqout));
  Full_Comparator full_comparator_9 (
    .a(a[7]), .b(b[7]), .gtin(full_comparator_7_gtout), .ltin(full_comparator_7_ltout),
    .eqin(full_comparator_7_eqout), .gtout(full_comparator_9_gtout), .ltout(full_comparator_9_ltout),
    .eqout(full_comparator_9_eqout));
  Full_Comparator full_comparator_10 (
    .a(a[5]), .b(b[5]), .gtin(full_comparator_8_gtout), .ltin(full_comparator_8_ltout),
    .eqin(full_comparator_8_eqout), .gtout(full_comparator_10_gtout), .ltout(full_comparator_10_ltout),
    .eqout(full_comparator_10_eqout));
  Full_Comparator full_comparator_11 (
    .a(a[4]), .b(b[4]), .gtin(full_comparator_10_gtout), .ltin(full_comparator_10_ltout),
    .eqin(full_comparator_10_eqout), .gtout(full_comparator_11_gtout), .ltout(full_comparator_11_ltout),
    .eqout(full_comparator_11_eqout));
  Full_Comparator full_comparator_12 (
    .a(a[3]), .b(b[3]), .gtin(full_comparator_11_gtout), .ltin(full_comparator_11_ltout),
    .eqin(full_comparator_11_eqout), .gtout(full_comparator_12_gtout), .ltout(full_comparator_12_ltout),
    .eqout(full_comparator_12_eqout));
  Full_Comparator full_comparator_13 (
    .a(a[2]), .b(b[2]), .gtin(full_comparator_12_gtout), .ltin(full_comparator_12_ltout),
    .eqin(full_comparator_12_eqout), .gtout(full_comparator_13_gtout), .ltout(full_comparator_13_ltout),
    .eqout(full_comparator_13_eqout));
  Full_Comparator full_comparator_14 (
    .a(a[1]), .b(b[1]), .gtin(full_comparator_13_gtout), .ltin(full_comparator_13_ltout),
    .eqin(full_comparator_13_eqout), .gtout(full_comparator_14_gtout), .ltout(full_comparator_14_ltout),
    .eqout(full_comparator_14_eqout));
  Full_Comparator full_comparator_15 (
    .a(a[0]), .b(b[0]), .gtin(full_comparator_14_gtout), .ltin(full_comparator_14_ltout),
    .eqin(full_comparator_14_eqout), .gtout(gt), .ltout(lt), .eqout(eq));
endmodule

module Register_File (
  input  [2:0] read_register,
  input  [2:0] write_register,
  input  [2:0] read_register2,
  input  write_enable,
  input  clock,
  input  [15:0] write_data,
  output [15:0] output_data,
  output [15:0] output_data2
);

  wire and_1_out, and_2_out, and_3_out, and_4_out, and_5_out, and_6_out, and_7_out, and_8_out,
       decoder_1_out0, decoder_1_out1, decoder_1_out2, decoder_1_out3, decoder_1_out4, decoder_1_out5,
       decoder_1_out6, decoder_1_out7;
  wire [15:0] register_1_q, register_2_q, register_3_q, register_4_q, register_5_q, register_6_q,
       register_7_q, register_8_q;

  Decoder #(.select(3)) decoder_1 (
    .out0(decoder_1_out0), .out1(decoder_1_out1), .out2(decoder_1_out2), .out3(decoder_1_out3),
    .out4(decoder_1_out4), .out5(decoder_1_out5), .out6(decoder_1_out6), .out7(decoder_1_out7),
    .sel(write_register));  // open: en
  and and_1 (and_1_out, decoder_1_out0, write_enable);
  and and_2 (and_2_out, decoder_1_out1, write_enable);
  and and_3 (and_3_out, decoder_1_out2, write_enable);
  and and_4 (and_4_out, decoder_1_out3, write_enable);
  and and_5 (and_5_out, decoder_1_out4, write_enable);
  and and_6 (and_6_out, decoder_1_out5, write_enable);
  and and_7 (and_7_out, decoder_1_out6, write_enable);
  and and_8 (and_8_out, decoder_1_out7, write_enable);
  Register #(.width(16)) register_1 (.D(write_data), .en(and_1_out), .Q(register_1_q), .clk(clock));  // open: clr
  Register #(.width(16)) register_2 (.D(write_data), .en(and_2_out), .Q(register_2_q), .clk(clock));  // open: clr
  Register #(.width(16)) register_3 (.D(write_data), .en(and_3_out), .Q(register_3_q), .clk(clock));  // open: clr
  Register #(.width(16)) register_4 (.D(write_data), .en(and_4_out), .Q(register_4_q), .clk(clock));  // open: clr
  Register #(.width(16)) register_5 (.D(write_data), .en(and_5_out), .Q(register_5_q), .clk(clock), .clr(clock));
  Register #(.width(16)) register_6 (.D(write_data), .en(and_6_out), .Q(register_6_q), .clk(clock));  // open: clr
  Register #(.width(16)) register_7 (.D(write_data), .en(and_7_out), .Q(register_7_q), .clk(clock));  // open: clr
  Register #(.width(16)) register_8 (.D(write_data), .en(and_8_out), .Q(register_8_q), .clk(clock));  // open: clr
  Multiplexer #(.select(3), .width(16)) multiplexer_1 (
    .in0(register_1_q), .in1(register_2_q), .in2(register_3_q), .in3(register_4_q), .in4(register_5_q),
    .in5(register_6_q), .in6(register_7_q), .in7(register_8_q), .out(output_data2), .sel(read_register2));  // open: en
  Multiplexer #(.select(3), .width(16)) multiplexer_2 (
    .in0(register_1_q), .in1(register_2_q), .in2(register_3_q), .in3(register_4_q), .in4(register_5_q),
    .in5(register_6_q), .in6(register_7_q), .in7(register_8_q), .out(output_data), .sel(read_register));  // open: en
  // Probe on output_data2
endmodule

module D_Latch (
  input  D,
  input  clock,
  input  enable,
  output Q
);

  wire and_1_out, and_2_out, nor_1_out, not_1_out;

  not not_1 (not_1_out, D);
  and and_1 (and_1_out, D, enable, clock);
  and and_2 (and_2_out, clock, enable, not_1_out);
  nor nor_1 (nor_1_out, and_1_out, Q);
  nor nor_2 (Q, nor_1_out, and_2_out);
endmodule

module D_Flip_Flop (
  input  D,
  input  clock,
  input  enable,
  output \output 
);

  wire d_latch_1_q, not_1_out;

  D_Latch d_latch_1 (.D(D), .clock(clock), .enable(enable), .Q(d_latch_1_q));
  not not_1 (not_1_out, clock);
  D_Latch d_latch_2 (.D(d_latch_1_q), .clock(not_1_out), .enable(enable), .Q(\output ));

  // Notes on the sheet:
  //   D Latch
  //   D Latch
endmodule

module _4_Bit_Register (
  input  enable,
  input  clock,
  input  [3:0] \input ,
  output [3:0] \output 
);

  D_Flip_Flop d_ff_1 (.D(\input [0]), .clock(clock), .enable(enable), .\output (\output [0]));
  D_Flip_Flop d_ff_2 (.D(\input [2]), .clock(clock), .enable(enable), .\output (\output [2]));
  D_Flip_Flop d_ff_3 (.D(\input [1]), .clock(clock), .enable(enable), .\output (\output [1]));
  D_Flip_Flop d_ff_4 (.D(\input [3]), .clock(clock), .enable(enable), .\output (\output [3]));

  // Notes on the sheet:
  //   D Flip-Flop
  //   D Flip-Flop
  //   D Flip-Flop
  //   D Flip-Flop
endmodule

module _16_Bit_Register (
  input  enable,
  input  clock,
  input  [15:0] \input ,
  output [15:0] \output 
);

  _4_Bit_Register u_4_bit_register_1 (.\input (\input [3:0]), .\output (\output [3:0]), .enable(enable), .clock(clock));
  _4_Bit_Register u_4_bit_register_2 (
    .\input (\input [11:8]), .\output (\output [11:8]), .enable(enable), .clock(clock));
  _4_Bit_Register u_4_bit_register_3 (.\input (\input [7:4]), .\output (\output [7:4]), .enable(enable), .clock(clock));
  _4_Bit_Register u_4_bit_register_4 (
    .\input (\input [15:12]), .\output (\output [15:12]), .enable(enable), .clock(clock));

  // Notes on the sheet:
  //   4-Bit Register
  //   4-Bit Register
  //   4-Bit Register
  //   4-Bit Register
  //   4-Bit Register
endmodule

module Control_Unit (
  input  JumpCheck,
  input  [15:0] Input,
  input  in_3,
  input  [15:0] CMPOP1,
  input  [15:0] CMPOP2,
  output JumpSignal,
  output ImmediateSignal,
  output instReadSignal,
  output [9:0] Jump_Address,
  output pcReadSignal,
  output ZF,
  output CF,
  output memWriteSignal,
  output Compare,
  output Load,
  output registerWriteSignal,
  output [9:0] LD_ST_Address,
  output [2:0] SR2,
  output [2:0] SR1,
  output [2:0] DST,
  output [1:0] out_21,
  output [2:0] OP1,
  output AluControl,
  output [2:0] OP2,
  output [15:0] Immediate_Address
);

  wire ADD, ADDI, AND, and_1_out, and_2_out, and_3_out, and_4_out, and_5_out, and_6_out, and_7_out,
       and_8_out, and_9_out, and_10_out, and_11_out, and_12_out, and_13_out, and_14_out, ANDI, JA, JAE, JB,
       JBE, JE, JMP, n16_bit_comparator_1_eq, n16_bit_comparator_1_gt, n16_bit_comparator_1_lt, or_3_out,
       or_4_out;

  Decoder #(.select(4)) decoder_1 (
    .out0(AND), .out1(ADD), .out2(ANDI), .out3(ADDI), .out4(Load), .out5(memWriteSignal), .out6(Compare),
    .out7(JMP), .out8(JE), .out9(JA), .out10(JB), .out11(JBE), .out12(JAE), .sel(Input[15:12]));  // open: out13, out14, out15, en
  // Priority_Encoder #(.select(2)) priority_encoder_1: pin names not known; wires that end beside it: AND, ADD, out_21, ANDI, AluControl, ADDI
  or or_1 (registerWriteSignal, AND, ADD, ANDI, ADDI, Load);
  assign LD_ST_Address = {{1{1'b0}}, Input[8:0]};  // Bit_Extender bit_extender_1
  assign Immediate_Address = {{10{1'b0}}, Input[5:0]};  // Bit_Extender bit_extender_2
  or or_2 (ImmediateSignal, ADDI, ANDI);
  not not_1 (instReadSignal, in_3);
  _16_Bit_Comparator u_16_bit_comparator_1 (
    .a(CMPOP1), .b(CMPOP2), .gt(n16_bit_comparator_1_gt), .lt(n16_bit_comparator_1_lt),
    .eq(n16_bit_comparator_1_eq));
  and and_1 (and_1_out, ~n16_bit_comparator_1_gt, n16_bit_comparator_1_eq, ~n16_bit_comparator_1_lt);  // AND_Gate
  and and_2 (and_2_out, ~n16_bit_comparator_1_gt, ~n16_bit_comparator_1_eq, n16_bit_comparator_1_lt);  // AND_Gate
  Register #(.width(1)) register_1 (.D(and_1_out), .en(Compare), .Q(ZF), .clk(in_3));  // open: clr
  Register #(.width(1)) register_2 (.D(and_2_out), .en(Compare), .Q(CF), .clk(in_3));  // open: clr
  and and_3 (and_3_out, ~ZF, CF);  // AND_Gate
  and and_4 (and_4_out, ZF, ~CF);  // AND_Gate
  and and_5 (and_5_out, ~ZF, ~CF);  // AND_Gate
  and and_6 (and_6_out, ZF, ~CF);  // AND_Gate
  and and_7 (and_7_out, ZF, ~CF);  // AND_Gate
  and and_8 (and_8_out, ~ZF, ~CF);  // AND_Gate
  and and_9 (and_9_out, ~ZF, CF);  // AND_Gate
  or or_3 (or_3_out, and_3_out, and_4_out);
  or or_4 (or_4_out, and_5_out, and_6_out);
  and and_10 (and_10_out, and_7_out, JE, JumpCheck);
  and and_11 (and_11_out, and_8_out, JA, JumpCheck);
  and and_12 (and_12_out, and_9_out, JB, JumpCheck);
  and and_13 (and_13_out, or_3_out, JBE, JumpCheck);
  and and_14 (and_14_out, or_4_out, JAE, JumpCheck);
  or or_5 (JumpSignal, and_10_out, and_11_out, and_12_out, and_13_out, and_14_out, JMP);

  assign DST = Input[11:9];
  assign Jump_Address = Input[9:0];
  assign OP1 = Input[8:6];
  assign OP2 = Input[2:0];
  assign pcReadSignal = in_3;
  assign SR1 = Input[8:6];
  assign SR2 = Input[2:0];

  // Other names for the same wires on the sheet: Clock = in_3; CMP = Compare; Jump[9:0] = Input[9:0];
  //   Immediate[5:0] = Input[5:0]; LD_ST[8:0] = Input[8:0]; Opcode[3:0] = Input[15:12]; LD = Load;
  //   ST = memWriteSignal

  // Notes on the sheet:
  //   16-Bit Comparator
endmodule

module PC_Register (
  input  [9:0] Jump_Address,
  input  AddressSelect,
  input  Enable,
  input  Clear,
  input  Clock,
  output [9:0] PC_Address
);

  wire [9:0] adder_1_out, multiplexer_1_out;

  Multiplexer #(.width(10)) multiplexer_1 (
    .in0(10'h1), .in1(Jump_Address), .out(multiplexer_1_out), .sel(AddressSelect));  // open: en
  Adder #(.width(10)) adder_1 (.a(multiplexer_1_out), .b(PC_Address), .out(adder_1_out));  // open: cin, cout
  Register #(.width(10)) register_1 (.D(adder_1_out), .en(Enable), .Q(PC_Address), .clk(Clock), .clr(Clear));
endmodule
